// Logisim project wk6ex1-4.circ as structural Verilog: 9 circuits, main circuit MyXOR
module MyXOR (
  input  x,
  input  y,
  output o
);

  wire and_1_out, and_2_out, not_1_out, not_2_out;

  not not_1 (not_1_out, y);
  not not_2 (not_2_out, x);
  and and_1 (and_1_out, x, not_1_out);
  and and_2 (and_2_out, not_2_out, y);
  or or_1 (o, and_1_out, and_2_out);

  // Notes on the sheet:
  //   Hier kan je een XOR-schakeling bouwen
  //   Je kan de tutorial volgen (in het Help-menu; "tutorial") of zelf de oplossing bedenken...
endmodule

module FullAdder (
  input  X,
  input  Y,
  input  CarryIn,
  output Sum,
  output CarryOut
);

  wire and_1_out, and_2_out, xor_1_out;

  xor xor_1 (xor_1_out, X, Y);
  xor xor_2 (Sum, xor_1_out, CarryIn);
  and and_1 (and_1_out, CarryIn, xor_1_out);
  and and_2 (and_2_out, X, Y);
  or or_1 (CarryOut, and_1_out, and_2_out);

  // Notes on the sheet:
  //   3 invoerbits:  X,  Y en CarryIn
  //   Hier kan je een FULL-ADDERschakeling bouwen
  //   (1) teken de andere vier rails   (2) je hebt 8 AND-poorten nodig    (3)  je hebt twee OR-poorten nodig
endmodule

module Een_4bit_Ripple_Carry_Adder (
  input  Y3,
  input  Y2,
  input  Y1,
  input  Y0,
  input  X3,
  input  X2,
  input  X1,
  input  X0,
  output Sum4,
  output Sum3,
  output Sum2,
  output Sum1,
  output Sum0
);

  wire fulladder_2_carryout, fulladder_3_carryout, fulladder_4_carryout;

  FullAdder fulladder_1 (.X(X3), .Y(Y3), .CarryIn(fulladder_2_carryout), .Sum(Sum3), .CarryOut(Sum4));
  FullAdder fulladder_2 (.X(X2), .Y(Y2), .CarryIn(fulladder_3_carryout), .Sum(Sum2), .CarryOut(fulladder_2_carryout));
  FullAdder fulladder_3 (.X(X1), .Y(Y1), .CarryIn(fulladder_4_carryout), .Sum(Sum1), .CarryOut(fulladder_3_carryout));
  FullAdder fulladder_4 (.X(X0), .Y(Y0), .CarryIn(1'b0), .Sum(Sum0), .CarryOut(fulladder_4_carryout));

  // Notes on the sheet:
  //   Hier kan je een 4-bit-RIPPLE-CARRY-ADDERschakeling bouwen
  //   8 invoerbits
  //   5 uitvoerbits
endmodule

module Een_4bit_vermenigvuldiger (
  input  Y0,
  input  Y1,
  input  Y2,
  input  Y3,
  input  X0,
  input  x1,
  input  X2,
  input  X3,
  output Z7,
  output Z6,
  output Z5,
  output Z4,
  output Z3,
  output Z2,
  output Z1,
  output Z0
);

  wire a_4by1_multiplier_1_z0, a_4by1_multiplier_1_z1, a_4by1_multiplier_1_z2, a_4by1_multiplier_1_z3,
       a_4by1_multiplier_2_z0, a_4by1_multiplier_2_z1, a_4by1_multiplier_2_z2, a_4by1_multiplier_2_z3,
       a_4by1_multiplier_3_z0, a_4by1_multiplier_3_z1, a_4by1_multiplier_3_z2, a_4by1_multiplier_3_z3,
       a_4by1_multiplier_4_z0, a_4by1_multiplier_4_z1, a_4by1_multiplier_4_z2,
       een_4bit_ripple_carry_adder_2_sum1, een_4bit_ripple_carry_adder_2_sum2,
       een_4bit_ripple_carry_adder_2_sum3, een_4bit_ripple_carry_adder_2_sum4,
       een_4bit_ripple_carry_adder_3_sum1, een_4bit_ripple_carry_adder_3_sum2,
       een_4bit_ripple_carry_adder_3_sum3, een_4bit_ripple_carry_adder_3_sum4;

  a_4by1_multiplier a_4by1_multiplier_1 (
    .y3(Y0), .y2(Y1), .y1(Y2), .y0(Y3), .x(X3), .z3(a_4by1_multiplier_1_z3), .z2(a_4by1_multiplier_1_z2),
    .z1(a_4by1_multiplier_1_z1), .z0(a_4by1_multiplier_1_z0));
  Een_4bit_Ripple_Carry_Adder een_4bit_ripple_carry_adder_1 (
    .Y3(a_4by1_multiplier_1_z0), .X3(a_4by1_multiplier_1_z1), .Y2(a_4by1_multiplier_1_z2),
    .X2(a_4by1_multiplier_1_z3), .Y1(een_4bit_ripple_carry_adder_2_sum4),
    .X1(een_4bit_ripple_carry_adder_2_sum3), .Y0(een_4bit_ripple_carry_adder_2_sum2),
    .X0(een_4bit_ripple_carry_adder_2_sum1), .Sum4(Z7), .Sum3(Z6), .Sum2(Z5), .Sum1(Z4), .Sum0(Z3));
  a_4by1_multiplier a_4by1_multiplier_2 (
    .y3(Y0), .y2(Y1), .y1(Y2), .y0(Y3), .x(X2), .z3(a_4by1_multiplier_2_z3), .z2(a_4by1_multiplier_2_z2),
    .z1(a_4by1_multiplier_2_z1), .z0(a_4by1_multiplier_2_z0));
  Een_4bit_Ripple_Carry_Adder een_4bit_ripple_carry_adder_2 (
    .Y3(a_4by1_multiplier_2_z0), .X3(a_4by1_multiplier_2_z1), .Y2(a_4by1_multiplier_2_z2),
    .X2(a_4by1_multiplier_2_z3), .Y1(een_4bit_ripple_carry_adder_3_sum4),
    .X1(een_4bit_ripple_carry_adder_3_sum3), .Y0(een_4bit_ripple_carry_adder_3_sum2),
    .X0(een_4bit_ripple_carry_adder_3_sum1), .Sum4(een_4bit_ripple_carry_adder_2_sum4),
    .Sum3(een_4bit_ripple_carry_adder_2_sum3), .Sum2(een_4bit_ripple_carry_adder_2_sum2),
    .Sum1(een_4bit_ripple_carry_adder_2_sum1), .Sum0(Z2));
  a_4by1_multiplier a_4by1_multiplier_3 (
    .y3(Y0), .y2(Y1), .y1(Y2), .y0(Y3), .x(x1), .z3(a_4by1_multiplier_3_z3), .z2(a_4by1_multiplier_3_z2),
    .z1(a_4by1_multiplier_3_z1), .z0(a_4by1_multiplier_3_z0));
  Een_4bit_Ripple_Carry_Adder een_4bit_ripple_carry_adder_3 (
    .Y3(a_4by1_multiplier_3_z0), .X3(a_4by1_multiplier_3_z1), .Y2(a_4by1_multiplier_3_z2),
    .X2(a_4by1_multiplier_3_z3), .Y1(1'b0), .X1(a_4by1_multiplier_4_z0), .Y0(a_4by1_multiplier_4_z1),
    .X0(a_4by1_multiplier_4_z2), .Sum4(een_4bit_ripple_carry_adder_3_sum4),
    .Sum3(een_4bit_ripple_carry_adder_3_sum3), .Sum2(een_4bit_ripple_carry_adder_3_sum2),
    .Sum1(een_4bit_ripple_carry_adder_3_sum1), .Sum0(Z1));
  a_4by1_multiplier a_4by1_multiplier_4 (
    .y3(Y0), .y2(Y1), .y1(Y2), .y0(Y3), .x(X0), .z3(Z0), .z2(a_4by1_multiplier_4_z2),
    .z1(a_4by1_multiplier_4_z1), .z0(a_4by1_multiplier_4_z0));

  // Notes on the sheet:
  //   factor (4 bits)
  //   output (8 bits)
  //   tweede factor (4 bits)
endmodule

module Een_3bij2_deler (
  input  Y2,
  input  Y1,
  input  Y0,
  input  X1,
  input  X0,
  output Z2,
  output Z1,
  output Z0,
  output Error
);

  wire and_4_out, and_7_out, and_9_out, and_10_out, and_11_out, nor_1_out, nor_2_out, not_1_out, not_2_out,
       or_1_out, or_2_out, or_3_out, or_4_out;

  // AND_Gate and_1 has open pins: in0=Y2, in1=and_9_out, out=open
  // AND_Gate and_2 has open pins: in0=Y2, in1=and_11_out, out=open
  or or_1 (or_1_out, 1'b0, 1'b0);
  or or_2 (or_2_out, 1'b0, 1'b0);
  or or_3 (or_3_out, 1'b0, 1'b0);
  // AND_Gate and_3 has open pins: in0=Y1, in1=and_9_out, out=open
  and and_4 (and_4_out, Y2, and_10_out);
  // AND_Gate and_5 has open pins: in0=Y1, in1=and_11_out, out=open
  or or_4 (or_4_out, Y0, Y1);
  or or_5 (Z2, or_1_out, 1'b0);
  or or_6 (Z1, or_2_out, 1'b0);
  or or_7 (Z0, or_3_out, 1'b0);
  // AND_Gate and_6 has open pins: in0=Y0, in1=and_9_out, out=open
  and and_7 (and_7_out, Y1, and_10_out);
  // AND_Gate and_8 has open pins: in0=Y0, in1=and_11_out, out=open
  nor nor_1 (nor_1_out, or_4_out, Y2);
  not not_1 (not_1_out, X1);
  and and_9 (and_9_out, not_1_out, X0);
  and and_10 (and_10_out, X1, not_2_out);
  not not_2 (not_2_out, X0);
  and and_11 (and_11_out, X1, X0);
  nor nor_2 (nor_2_out, X0, X1);
  or or_8 (Error, nor_2_out, nor_1_out);

  // Notes on the sheet:
  //   Teller (3 bits: Y2 Y1 Y0)
  //   div_1
  //   div_2
  //   div_3
  //   Noemer (2 bits: X1 X0)
  //   Quotiënt (4 bits: Z2 Z1 Z0 en Error)
  //   3-bij-2-bit-DELINGSschakeling
endmodule

module Een_2bit_decoder (
);


  // Notes on the sheet:
  //   2-bit-DECODERschakeling (bonusopgave)
endmodule

module Een_12nGb_geheugen (
);


  // Notes on the sheet:
  //   12-nanogigabit-GEHEUGENschakelin (bonusopgave)
endmodule

module a_4by1_multiplier (
  input  y3,
  input  y2,
  input  y1,
  input  y0,
  input  x,
  output z3,
  output z2,
  output z1,
  output z0
);

  and and_1 (z3, x, y3);
  and and_2 (z2, x, y2);
  and and_3 (z1, x, y1);
  and and_4 (z0, x, y0);
endmodule

module subtractor_3by2 (
  input  x0,
  input  x1,
  input  x2,
  input  s0,
  input  s1,
  output o0,
  output o1,
  output o2
);

  FullAdder fulladder_1 (.X(x0));  // open: Y, CarryIn, Sum, CarryOut
endmodule
